# Fritzing sketch thesis_sketch (saved by Fritzing 0.7.10b)
breadboards: 1

parts:
  Arduino1 = Arduino
  T1 = LM35 Temperature Sensor [package="TO92 [THT]"]
  R1 = Resistor [tolerance=±5% resistance=220 package=THT]
  R2 = Photocell (LDR) [package=THT]
  Ultra_sound_sensor1 = ultrasound_sensor

nets:
  GND: Arduino1.GND, T1.GND, R1.Pin_0, Ultra_sound_sensor1.aún_sin_nombre#6
  N1: Arduino1.+5V, T1.+Vs, R2.pin_0, Ultra_sound_sensor1.aún_sin_nombre#5
  N2: Arduino1.A3, Ultra_sound_sensor1.aún_sin_nombre#2
  N3: Arduino1.A4, R1.Pin_1, R2.pin_1
  N4: Arduino1.A5, T1.Vout
